// Logisim project relatorios.circ as structural Verilog: 11 circuits, main circuit main
module main (
  input  [1:0] in_1,
  input  in_2,
  output [1:0] out_3
);

  wire [1:0] demultiplexer_1_out0, demultiplexer_1_out1, meiosomador_1_s, meiosubtrator_1_s;

  Demultiplexer #(.width(2), .enable("false")) demultiplexer_1 (
    .out0(demultiplexer_1_out0), .out1(demultiplexer_1_out1), .in(in_1), .sel(in_2));
  meioSubtrator meiosubtrator_1 (
    .A(demultiplexer_1_out1[0]), .BOUT(meiosubtrator_1_s[1]), .B(demultiplexer_1_out1[1]),
    .S(meiosubtrator_1_s[0]));
  meioSomador meiosomador_1 (
    .COUT(meiosomador_1_s[1]), .S(meiosomador_1_s[0]), .B(demultiplexer_1_out0[1]),
    .A(demultiplexer_1_out0[0]));
  Multiplexer #(.width(2), .enable("false")) multiplexer_1 (
    .in0(meiosomador_1_s), .in1(meiosubtrator_1_s), .out(out_3), .sel(in_2));
endmodule

module meioSomador (
  input  A,
  input  B,
  output S,
  output COUT
);

  xor xor_1 (S, B, A);
  and and_1 (COUT, A, B);
endmodule

module meioSubtrator (
  input  A,
  input  B,
  output S,
  output BOUT
);

  xor xor_1 (S, A, B);
  and and_1 (BOUT, B, ~A);  // AND_Gate
endmodule

module somadorCompleto (
  input  A,
  input  B,
  input  CARRY_IN,
  output SOMA,
  output CARRY_OUT
);

  wire meiosomador_1_cout, meiosomador_1_s, meiosomador_2_cout;

  meioSomador meiosomador_1 (.COUT(meiosomador_1_cout), .S(meiosomador_1_s), .B(B), .A(A));
  meioSomador meiosomador_2 (.COUT(meiosomador_2_cout), .S(SOMA), .B(CARRY_IN), .A(meiosomador_1_s));
  or or_1 (CARRY_OUT, meiosomador_2_cout, meiosomador_1_cout);
endmodule

module EXERC2 (
  input  [2:0] in_1,
  input  in_2,
  output [1:0] out_3
);

  wire [1:0] somadorcompleto_1_carry_out, subtratorcompleto_1_bout;
  wire [2:0] demultiplexer_1_out0, demultiplexer_1_out1;

  Demultiplexer #(.width(3), .enable("false")) demultiplexer_1 (
    .out0(demultiplexer_1_out0), .out1(demultiplexer_1_out1), .in(in_1), .sel(in_2));
  somadorCompleto somadorcompleto_1 (
    .CARRY_OUT(somadorcompleto_1_carry_out[0]), .CARRY_IN(demultiplexer_1_out0[0]),
    .A(demultiplexer_1_out0[2]), .B(demultiplexer_1_out0[1]), .SOMA(somadorcompleto_1_carry_out[1]));
  subtratorCompleto subtratorcompleto_1 (
    .S(subtratorcompleto_1_bout[1]), .B(demultiplexer_1_out1[1]), .BIN(demultiplexer_1_out1[0]),
    .BOUT(subtratorcompleto_1_bout[0]), .A(demultiplexer_1_out1[2]));
  Multiplexer #(.width(2), .enable("false")) multiplexer_1 (
    .in0(somadorcompleto_1_carry_out), .in1(subtratorcompleto_1_bout), .out(out_3), .sel(in_2));
endmodule

module subtratorCompleto (
  input  A,
  input  B,
  input  BIN,
  output S,
  output BOUT
);

  wire meiosubtrator_1_bout, meiosubtrator_1_s, meiosubtrator_2_bout;

  meioSubtrator meiosubtrator_1 (.A(A), .BOUT(meiosubtrator_1_bout), .B(B), .S(meiosubtrator_1_s));
  meioSubtrator meiosubtrator_2 (.A(meiosubtrator_1_s), .BOUT(meiosubtrator_2_bout), .B(BIN), .S(S));
  or or_1 (BOUT, meiosubtrator_2_bout, meiosubtrator_1_bout);
endmodule

module multiplicador (
  input  A1,
  input  A0,
  input  B1,
  input  B0,
  output P3,
  output P2,
  output P1,
  output P0
);

  wire and_1_out, and_2_out, and_3_out, meiosomador_2_cout;

  and and_1 (and_1_out, A1, B1);
  meioSomador meiosomador_1 (.COUT(P3), .S(P2), .B(and_1_out), .A(meiosomador_2_cout));
  and and_2 (and_2_out, A1, B0);
  meioSomador meiosomador_2 (.COUT(meiosomador_2_cout), .S(P1), .B(and_2_out), .A(and_3_out));
  and and_3 (and_3_out, A0, B1);
  and and_4 (P0, A0, B0);
endmodule

module Registradordesloc (
  input  [3:0] D,
  input  CLOCK,
  input  CARGA,
  input  CLEAR,
  output [3:0] Q
);

  wire multiplexer_1_out, multiplexer_2_out, multiplexer_3_out, multiplexer_4_out;

  Multiplexer #(.enable("false")) multiplexer_1 (.in0(Q[3]), .in1(D[3]), .out(multiplexer_1_out), .sel(CARGA));
  D_Flip_Flop d_ff_1 (.D(multiplexer_1_out), .clk(CLOCK), .Q(Q[3]), .reset(CLEAR));  // open: Qn, preset
  Multiplexer #(.enable("false")) multiplexer_2 (.in0(Q[2]), .in1(D[2]), .out(multiplexer_2_out), .sel(CARGA));
  D_Flip_Flop d_ff_2 (.D(multiplexer_2_out), .clk(CLOCK), .Q(Q[2]), .reset(CLEAR));  // open: Qn, preset
  Multiplexer #(.enable("false")) multiplexer_3 (.in0(Q[1]), .in1(D[1]), .out(multiplexer_3_out), .sel(CARGA));
  D_Flip_Flop d_ff_3 (.D(multiplexer_3_out), .clk(CLOCK), .Q(Q[1]), .reset(CLEAR));  // open: Qn, preset
  Multiplexer #(.enable("false")) multiplexer_4 (.in0(Q[0]), .in1(D[0]), .out(multiplexer_4_out), .sel(CARGA));
  D_Flip_Flop d_ff_4 (.D(multiplexer_4_out), .clk(CLOCK), .Q(Q[0]), .reset(CLEAR));  // open: Qn, preset
endmodule

module subtratorC_8bits (
  input  [7:0] A,
  input  [7:0] B,
  output [7:0] S,
  output BOUT
);

  wire subtratorcompleto_1_bout, subtratorcompleto_2_bout, subtratorcompleto_3_bout,
       subtratorcompleto_4_bout, subtratorcompleto_5_bout, subtratorcompleto_6_bout, subtratorcompleto_7_bout;

  subtratorCompleto subtratorcompleto_1 (.S(S[0]), .B(B[0]), .BIN(1'b0), .BOUT(subtratorcompleto_1_bout), .A(A[0]));
  subtratorCompleto subtratorcompleto_2 (
    .S(S[1]), .B(B[1]), .BIN(subtratorcompleto_1_bout), .BOUT(subtratorcompleto_2_bout), .A(A[1]));
  subtratorCompleto subtratorcompleto_3 (
    .S(S[2]), .B(B[2]), .BIN(subtratorcompleto_2_bout), .BOUT(subtratorcompleto_3_bout), .A(A[2]));
  subtratorCompleto subtratorcompleto_4 (
    .S(S[3]), .B(B[3]), .BIN(subtratorcompleto_3_bout), .BOUT(subtratorcompleto_4_bout), .A(A[3]));
  subtratorCompleto subtratorcompleto_5 (
    .S(S[4]), .B(B[4]), .BIN(subtratorcompleto_4_bout), .BOUT(subtratorcompleto_5_bout), .A(A[4]));
  subtratorCompleto subtratorcompleto_6 (
    .S(S[5]), .B(B[5]), .BIN(subtratorcompleto_5_bout), .BOUT(subtratorcompleto_6_bout), .A(A[5]));
  subtratorCompleto subtratorcompleto_7 (
    .S(S[6]), .B(B[6]), .BIN(subtratorcompleto_6_bout), .BOUT(subtratorcompleto_7_bout), .A(A[6]));
  subtratorCompleto subtratorcompleto_8 (.S(S[7]), .B(B[7]), .BIN(subtratorcompleto_7_bout), .BOUT(BOUT), .A(A[7]));
endmodule

module somadorC_8bits (
  input  [7:0] B,
  input  [7:0] A,
  output [7:0] S,
  output COUT
);

  wire somadorcompleto_1_carry_out, somadorcompleto_2_carry_out, somadorcompleto_3_carry_out,
       somadorcompleto_4_carry_out, somadorcompleto_5_carry_out, somadorcompleto_6_carry_out,
       somadorcompleto_7_carry_out;

  somadorCompleto somadorcompleto_1 (
    .CARRY_OUT(somadorcompleto_1_carry_out), .CARRY_IN(1'b0), .A(A[0]), .B(B[0]), .SOMA(S[0]));
  somadorCompleto somadorcompleto_2 (
    .CARRY_OUT(somadorcompleto_2_carry_out), .CARRY_IN(somadorcompleto_1_carry_out), .A(A[1]), .B(B[1]),
    .SOMA(S[1]));
  somadorCompleto somadorcompleto_3 (
    .CARRY_OUT(somadorcompleto_3_carry_out), .CARRY_IN(somadorcompleto_2_carry_out), .A(A[2]), .B(B[2]),
    .SOMA(S[2]));
  somadorCompleto somadorcompleto_4 (
    .CARRY_OUT(somadorcompleto_4_carry_out), .CARRY_IN(somadorcompleto_3_carry_out), .A(A[3]), .B(B[3]),
    .SOMA(S[3]));
  somadorCompleto somadorcompleto_5 (
    .CARRY_OUT(somadorcompleto_5_carry_out), .CARRY_IN(somadorcompleto_4_carry_out), .A(A[4]), .B(B[4]),
    .SOMA(S[4]));
  somadorCompleto somadorcompleto_6 (
    .CARRY_OUT(somadorcompleto_6_carry_out), .CARRY_IN(somadorcompleto_5_carry_out), .A(A[5]), .B(B[5]),
    .SOMA(S[5]));
  somadorCompleto somadorcompleto_7 (
    .CARRY_OUT(somadorcompleto_7_carry_out), .CARRY_IN(somadorcompleto_6_carry_out), .A(A[6]), .B(B[6]),
    .SOMA(S[6]));
  somadorCompleto somadorcompleto_8 (
    .CARRY_OUT(COUT), .CARRY_IN(somadorcompleto_7_carry_out), .A(A[7]), .B(B[7]), .SOMA(S[7]));
endmodule

module projeto1 (
  input  [7:0] A,
  input  [7:0] B,
  input  [2:0] d,
  input  [3:0] OPCODE,
  input  [2:0] d2,
  output [7:0] S,
  output COUT,
  output BOUT
);

  wire [7:0] and_1_out, multiplier_1_out, nand_1_out, nor_1_out, not_1_out, or_1_out, shifter_1_out,
       shifter_2_out, somadorc_8bits_1_s, subtratorc_8bits_1_s, xnor_1_out, xor_1_out;

  Multiplier multiplier_1 (.a(A), .b(B), .out(multiplier_1_out));  // open: cin, cout
  assign and_1_out = A & B;  // AND_Gate and_1, 8 bits wide
  assign xor_1_out = A ^ B;  // XOR_Gate xor_1, 8 bits wide
  Shifter #(.shift("lr")) shifter_1 (.in(A), .\dist (d), .out(shifter_1_out));
  Shifter shifter_2 (.in(A), .\dist (d2), .out(shifter_2_out));
  assign or_1_out = A | B;  // OR_Gate or_1, 8 bits wide
  assign xnor_1_out = ~(A ^ B);  // XNOR_Gate xnor_1, 8 bits wide
  somadorC_8bits somadorc_8bits_1 (.COUT(COUT), .S(somadorc_8bits_1_s), .A(A), .B(B));
  subtratorC_8bits subtratorc_8bits_1 (.BOUT(BOUT), .S(subtratorc_8bits_1_s), .B(B), .A(A));
  assign nand_1_out = ~(A & B);  // NAND_Gate nand_1, 8 bits wide
  assign nor_1_out = ~(A | B);  // NOR_Gate nor_1, 8 bits wide
  assign not_1_out = ~A;  // NOT_Gate not_1, 8 bits wide
  Multiplexer #(.select(4), .width(8), .enable("false")) multiplexer_1 (
    .in1(nor_1_out), .in2(not_1_out), .in3({8{1'b0}}), .in4(nand_1_out), .in5(shifter_1_out),
    .in6({8{1'b0}}), .in7(xor_1_out), .in8(multiplier_1_out), .in9(and_1_out), .in10(shifter_2_out),
    .in11(xnor_1_out), .in12(somadorc_8bits_1_s), .in13({8{1'b0}}), .in14(or_1_out),
    .in15(subtratorc_8bits_1_s), .out(S), .sel(OPCODE));  // open: in0
endmodule
